# Fritzing sketch Circuit (saved by Fritzing 0.9.3b)

parts:
  Raspberry_Pi_1 = Raspberry Pi 3 [part_number=RPI-3-V1.2]
  PIR1 = PIR sensor

nets:
  N1: Raspberry_Pi_1.GPIO17, PIR1.SIG
  GND: Raspberry_Pi_1.GND, PIR1.GND
  5V: Raspberry_Pi_1.5V, PIR1.VDD

notes:
  Insert Pi camera with blue tab facing the Ethernet port.
